# Fritzing sketch attic-fan (saved by Fritzing 0.9.1b)
breadboards: 1

parts:
  Part1 = Arduino Uno (Rev3)
  R1 = Rotary Potentiometer (Small) [maximum_resistance=100kΩ package=THT]
  DHT1 = DHT22 Humidity and Temperature Sensor
  J1 = Basic Servo
  OLED1 = 128x64 I2C Monochrome OLED Display

nets:
  N1: Part1.A0, R1.wiper
  N2: Part1.D9_PWM, J1.pulse
  N3: Part1.A4/SDA, OLED1.SDA
  N4: Part1.D2, DHT1.DATA
  5V: Part1.5V, R1.leg1, DHT1.VDD, J1.vcc
  GND: Part1.GND, R1.leg2, DHT1.GND, J1.gnd

custom parts:
  128x64 I2C Monochrome OLED Display: 128x32 I2C Monochrome OLED Display
